// Digital circuit InstDecoder.dig as structural Verilog
module InstDecoder (
  input  [31:0] IW,
  output [1:0] ALUSrcB,
  output [2:0] ALUOp,
  output RFW,
  output WDsel,
  output PCsel,
  output ALUSrcA
);

  wire addi_1_eq, addr_1_eq, j_type_eq, jalr_1_eq, mul_1_eq, sll_1_r, slli_1_r, srl_1_eq, srli_1_r, sub_1_r;
  wire [3:0] INUM_num;

  ADDI addi_1 (.iw_opcode(IW[6:0]), .iw_funct3(IW[14:12]), .eq(addi_1_eq));
  ADDR addr_1 (.iw_opcode(IW[6:0]), .iw_funct3(IW[14:12]), .iw_funct7(IW[31:25]), .eq(addr_1_eq));
  Comparator #(.Bits(7)) j_type (.a(IW[6:0]), .b(7'b1101111), .eq(j_type_eq));  // open: gt, lt
  JALR jalr_1 (.iw_opcode(IW[6:0]), .iw_funct3(IW[14:12]), .eq(jalr_1_eq));
  MUL mul_1 (.OPC(IW[6:0]), .funct3(IW[14:12]), .funct7(IW[31:25]), .eq(mul_1_eq));
  SUB sub_1 (.OPC(IW[6:0]), .funct3(IW[14:12]), .funct7(IW[31:25]), .R(sub_1_r));
  SLL sll_1 (.OPC(IW[6:0]), .funct3(IW[14:12]), .funct7(IW[31:25]), .R(sll_1_r));
  SRL srl_1 (.OPC(IW[6:0]), .funct3(IW[14:12]), .funct7(IW[31:25]), .eq(srl_1_eq));
  SLLI slli_1 (.OPC(IW[6:0]), .funct3(IW[14:12]), .funct7(IW[31:25]), .R(slli_1_r));
  SRLI srli_1 (.OPC(IW[6:0]), .funct3(IW[14:12]), .funct7(IW[31:25]), .R(srli_1_r));
  PriorityEncoder #(.Selector_Bits(4)) INUM (
    .in0(addi_1_eq), .in1(addr_1_eq), .in2(j_type_eq), .in3(jalr_1_eq), .in4(mul_1_eq), .in5(sub_1_r),
    .in6(sll_1_r), .in7(srl_1_eq), .in8(slli_1_r), .in9(srli_1_r), .in10(1'b0), .in11(1'b0), .in12(1'b0),
    .in13(1'b0), .in14(1'b0), .in15(1'b0), .num(INUM_num));  // open: any
  ROM #(.AddrBits(4), .Bits(9)) rom_1 (.A(INUM_num), .sel(1'b1), .D({RFW, ALUOp, ALUSrcA, ALUSrcB, PCsel, WDsel}));

  // Other names for the same wires on the sheet: iw_opcode[6:0] = IW[6:0]; iw_f3[2:0] = IW[14:12];
  //   iw_f7[6:0] = IW[31:25]

  // Notes on the sheet:
  //   contents of rom_1 (hex, n*v repeats v):
  //   104,100,11b,107,140,120,160,180,1a4,1c4
endmodule
