// Digital circuit alu.dig as structural Verilog
module alu (
  input  [63:0] A,
  input  [63:0] B,
  input  [2:0] ALUOp,
  output [63:0] R
);

  wire [63:0] add_1_s, div_1_q, mul_1_mul, sub_1_s;

  Add #(.Bits(64)) add_1 (.a(A), .b(B), .c_i(1'b0), .s(add_1_s));  // open: c_o
  Sub #(.Bits(64)) sub_1 (.a(A), .b(B), .c_i(1'b0), .s(sub_1_s));  // open: c_o
  Mul #(.Bits(32)) mul_1 (.a(A[31:0]), .b(B[31:0]), .mul(mul_1_mul));
  Div #(.Bits(64)) div_1 (.a(A), .b(B), .q(div_1_q));  // open: r
  Multiplexer #(.Selector_Bits(3), .Bits(64)) multiplexer_1 (
    .sel(ALUOp), .in_0(add_1_s), .in_1(sub_1_s), .in_2(mul_1_mul), .in_3(div_1_q), .in_4({64{1'b0}}),
    .in_5({64{1'b0}}), .in_6({64{1'b0}}), .in_7({64{1'b0}}), .out(R));
endmodule
